# Fritzing sketch spica (saved by Fritzing 0.9.3b)
circuit board: 8.46667cm x 5.64444cm
breadboards: 1

parts:
  U1 = ESP32S-HiLetgo [part_number=ESP32S-HiLetgo]
  IC1 = V_REG_LD1117VXX [package=78xxl]
  C1 = Ceramic Capacitor [capacitance=0.1µF voltage=6.3V package="100 mil [THT, multilayer]"]
  C2 = Electrolytic Capacitor [capacitance=100µF package="100 mil [THT, electrolytic]"]
  C3 = Electrolytic Capacitor [capacitance=1mF voltage=10V package="100 mil [THT, electrolytic]"]
  IC2 = AE-DRV8835-S [package="DIP (Dual Inline) [THT]"]
  VCC2 = Battery

nets:
  N1: U1.3.3, IC1.OUT, C2.+, IC2.VCC
  GND: U1.GND, IC1.GND, C1.0, C2.-, C3.-, IC2.GND, VCC2.-
  N2: IC1.IN, C1.1, C3.+, VCC2.+

custom parts:
  ESP32S-HiLetgo: HiLetgo ESP-WROOM-32 ESP32 ESP-32S Development Board 2.4GHz Dual-Mode WiFi + Bluetooth Dual Cores Microcontroller The ESP32 integrated with Antenna switches, RF Balun, power amplifiers, low-noise amplifiers, filters, and management modules, and the entire solution occupies the least area of PCB. 2.4 GHz Wi-Fi plus Bluetooth dual-mode chip, with TSMC Ultra-low power consumption 40nm technology,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
  AE-DRV8835-S: A DRV8835 breakout board by Akizuki Denshi Tsusho Co.,Ltd.
